# Fritzing sketch Distance Alarm (saved by Fritzing 1.0.5)
breadboards: 1

parts:
  Mod1 = Raspberry Pi Pico
  HC-SR04_Sensor_1 = HC-SR04 Ultrasonic Distance Sensor

nets:
  N1: Mod1.pin_3, Mod1.pin_8, Mod1.pin_13, Mod1.pin_18, Mod1.pin_23, Mod1.pin_28, Mod1.pin_33, Mod1.pin_38, Mod1.pin_42, HC-SR04_Sensor_1.GND
  N2: Mod1.pin_4, HC-SR04_Sensor_1.TRIG
  N3: Mod1.pin_5, HC-SR04_Sensor_1.ECHO
  N4: Mod1.pin_36, HC-SR04_Sensor_1.VCC

notes:
  LCD DRIVER
  GND --> Ground
  VCC --> 3V3
  SDA --> GPIO 0
  SCL --> GPIO 1

custom parts:
  Raspberry Pi Pico: Raspberry Pi Pico. Based around the RP2040 microcontroller the Pico is a low cost microcontroller device bringing Raspberry Pi quality, cost, and easy of use to the microcontroller space. Jan 2021, Split part in to two versions: SMD (this one) and tht. This one is single sided and uses the castellation pads to solder the module to the board (no holes, other than for the USB connector!). The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
